// Logisim project cache.circ as structural Verilog: 1 circuit, main circuit cache
module cache (
  input  [13:0] CPU_Address,
  input  [31:0] code,
  input  CLOCK,
  input  RESET
);

  wire and_2_out, and_4_out, b_lock_1_hit, b_lock_2_hit, b_lock_3_hit, b_lock_4_hit, b_lock_5_hit,
       b_lock_6_hit, b_lock_7_hit, b_lock_8_hit, Hit, or_1_out, or_2_out, or_3_out, or_4_out, set1, set2,
       set3, set4;

  Register #(.width(10)) register_1 (.en(1'b1));  // open: D, clk, Q, clr
  Register #(.width(10)) register_2 (.en(1'b1));  // open: D, clk, Q, clr
  // AND_Gate and_1 has open pins: in0=CLOCK, in1=set1, out=open
  Decoder #(.select(2)) decoder_1 (
    .out0(set1), .out1(set2), .out2(set3), .out3(set4), .sel(CPU_Address[11:10]), .en(1'b1));
  B_lock b_lock_1 (
    .data_in(code), .word_index(CPU_Address[13:12]), .RESET(RESET), .hit(b_lock_1_hit));  // open: CLOCK, miss
  B_lock b_lock_2 (
    .data_in(code), .word_index(CPU_Address[13:12]), .RESET(RESET), .hit(b_lock_2_hit));  // open: CLOCK, miss
  or or_1 (or_1_out, b_lock_2_hit, b_lock_1_hit);
  and and_2 (and_2_out, CLOCK, set2);
  Register #(.width(10)) register_3 (.en(1'b1));  // open: D, clk, Q, clr
  Register #(.width(10)) register_4 (.en(1'b1));  // open: D, clk, Q, clr
  B_lock b_lock_3 (
    .data_in(code), .word_index(CPU_Address[13:12]), .RESET(RESET), .hit(b_lock_3_hit));  // open: CLOCK, miss
  B_lock b_lock_4 (
    .data_in(code), .word_index(CPU_Address[13:12]), .RESET(RESET), .hit(b_lock_4_hit));  // open: CLOCK, miss
  or or_2 (or_2_out, b_lock_4_hit, b_lock_3_hit);
  // AND_Gate and_3 has open pins: in0=CLOCK, in1=set3, out=open
  Register #(.width(10)) register_5 (.en(1'b1));  // open: D, clk, Q, clr
  Register #(.width(10)) register_6 (.en(1'b1));  // open: D, clk, Q, clr
  B_lock b_lock_5 (
    .data_in(code), .word_index(CPU_Address[13:12]), .RESET(RESET), .hit(b_lock_5_hit));  // open: CLOCK, miss
  B_lock b_lock_6 (
    .data_in(code), .word_index(CPU_Address[13:12]), .RESET(RESET), .hit(b_lock_6_hit));  // open: CLOCK, miss
  or or_3 (or_3_out, b_lock_6_hit, b_lock_5_hit);
  and and_4 (and_4_out, CLOCK, set4);
  Register #(.width(10)) register_7 (.en(1'b1));  // open: D, clk, Q, clr
  Register #(.width(10)) register_8 (.en(1'b1));  // open: D, clk, Q, clr
  B_lock b_lock_7 (
    .data_in(code), .word_index(CPU_Address[13:12]), .RESET(RESET), .hit(b_lock_7_hit));  // open: CLOCK, miss
  B_lock b_lock_8 (
    .data_in(code), .word_index(CPU_Address[13:12]), .RESET(RESET), .hit(b_lock_8_hit));  // open: CLOCK, miss
  or or_4 (or_4_out, b_lock_8_hit, b_lock_7_hit);
  or or_5 (Hit, or_4_out, or_3_out, or_2_out, or_1_out);

  // Other names for the same wires on the sheet: tag[9:0] = CPU_Address[9:0]; set[1:0] = CPU_Address[11:10];
  //   word_index[1:0] = CPU_Address[13:12]

  // Notes on the sheet:
  //   tag: 10 bit, set: 2bit, word: 2bit
  //   tag0
  //   tag1
  //   set1
  //   works: dirty bit/ tag bits/ transfering beetwin m.m and c.m and cpu 
  //   tag0
  //   tag1
  //   set2
  //   tag0
  //   tag1
  //   se3
  //   tag0
  //   tag1
  //   se4
endmodule
