// Logisim project cpu.circ as structural Verilog: 1 circuit, main circuit cpu
module cpu (
);

  wire ALU_main_zero, ALU_v, ALUSrc, and_1_out, Branch, clock_1_out, JAL, Jump, MemToReg, not_1_out, RegDst,
       RegWrite, syscall;
  wire [3:0] MemWriteMask;
  wire [4:0] instSplitter_rd, instSplitter_rs, instSplitter_rt, instSplitter_shamt, multiplexer_2_out,
       multiplexer_3_out;
  wire [5:0] ALU_op, instSplitter_func, instSplitter_op;
  wire [15:0] instSplitter_imm16;
  wire [25:0] instSplitter_target26;
  wire [27:0] SXL_2_t28;
  wire [31:0] adder_1_out, adder_2_out, ALU_main_aluresult, DataMem_memreaddata, instMem_memreaddata,
       jcu_1_y, multiplexer_1_out, multiplexer_4_out, multiplexer_5_out, multiplexer_6_out, PC_pc_out,
       RegisterFile_readdata1, RegisterFile_readdata2, SE_s32, shifter_1_out;

  Clock clock_1 (.out(clock_1_out));
  not not_1 (not_1_out, syscall);
  ProgramCounter PC (.PC_in(jcu_1_y), .En(not_1_out), .CLK(clock_1_out), .PC_out(PC_pc_out));
  Adder #(.width(32)) adder_1 (.a(PC_pc_out), .b(32'h4), .out(adder_1_out));  // open: cin, cout
  Multiplexer #(.width(32)) multiplexer_1 (
    .in0(multiplexer_5_out), .in1({adder_1_out[31:28], SXL_2_t28}), .out(multiplexer_1_out), .sel(Jump));
  memDelayed instMem (
    .MemAddress(PC_pc_out), .clk(clock_1_out), .MemReadData(instMem_memreaddata));  // open: MemWriteMask, MemWriteData
  SXL2 SXL_2 (.T26(instSplitter_target26), .T28(SXL_2_t28));
  instruction_splitter instSplitter (
    .instruction(instMem_memreaddata), .op(instSplitter_op), .target26(instSplitter_target26),
    .rs(instSplitter_rs), .rt(instSplitter_rt), .imm16(instSplitter_imm16), .rd(instSplitter_rd),
    .shamt(instSplitter_shamt), .func(instSplitter_func));
  Multiplexer #(.width(5)) multiplexer_2 (
    .in0(instSplitter_rt), .in1(instSplitter_rd), .out(multiplexer_2_out), .sel(RegDst));
  Multiplexer #(.width(5)) multiplexer_3 (.in0(multiplexer_2_out), .in1({5{1'b1}}), .out(multiplexer_3_out), .sel(JAL));
  JCU jcu_1 (.Func(instSplitter_func), .in1(multiplexer_1_out), .rs(instSplitter_rs), .Y(jcu_1_y));
  Multiplexer #(.width(32)) multiplexer_4 (.in0(multiplexer_6_out), .in1(jcu_1_y), .out(multiplexer_4_out), .sel(JAL));
  CU ControlUnit (
    .Func(instSplitter_func), .Opcode(instSplitter_op), .JAL(JAL), .ALUSrc(ALUSrc), .ALUop(ALU_op),
    .syscall(syscall), .RegDst(RegDst), .ALU_V(ALU_v), .MemToReg(MemToReg), .RegWrite(RegWrite),
    .MemWriteMask(MemWriteMask), .Branch(Branch), .Jump(Jump));
  SignExtend SE (.S16(instSplitter_imm16), .S32(SE_s32));
  regfile RegisterFile (
    .ReadIndex1(instSplitter_rs), .ReadIndex2(instSplitter_rt), .WriteIndex(multiplexer_3_out),
    .WriteData(multiplexer_4_out), .RegWEn(RegWrite), .clk(clock_1_out), .ReadData1(RegisterFile_readdata1),
    .ReadData2(RegisterFile_readdata2));
  Multiplexer #(.width(32)) multiplexer_5 (
    .in0(adder_1_out), .in1(adder_2_out), .out(multiplexer_5_out), .sel(and_1_out));
  Shifter #(.width(32)) shifter_1 (.in(SE_s32), .\dist (5'b00010), .out(shifter_1_out));
  Adder #(.width(32)) adder_2 (.a(adder_1_out), .b(shifter_1_out), .out(adder_2_out));  // open: cin, cout
  and and_1 (and_1_out, Branch, ALU_main_zero);
  ALU ALU_main (
    .A(RegisterFile_readdata1), .B(RegisterFile_readdata2), .ALUOp(ALU_op), .Func(instSplitter_func),
    .Imm(SE_s32), .Shamt(instSplitter_shamt), .ALUSrc(ALUSrc), .Zero(ALU_main_zero),
    .ALUResult(ALU_main_aluresult));
  memDelayed DataMem (
    .MemAddress(ALU_main_aluresult), .MemWriteMask(MemWriteMask), .MemWriteData(RegisterFile_readdata2),
    .clk(clock_1_out), .MemReadData(DataMem_memreaddata));
  Multiplexer #(.width(32)) multiplexer_6 (
    .in0(ALU_main_aluresult), .in1(DataMem_memreaddata), .out(multiplexer_6_out), .sel(MemToReg));
endmodule
